// Logisim project Pipelining.circ as structural Verilog: 1 circuit, main circuit main
module main (
);

  wire clock_1_out;
  wire [1:0] register_5_q, register_9_q;
  wire [2:0] register_4_q;
  wire [3:0] register_8_q, register_12_q, register_14_q;
  wire [7:0] alu_1_f, register_1_q, register_6_q, register_7_q, register_10_q, register_11_q, register_13_q,
       register_file_1_read_data_1, register_file_1_read_data_2;
  wire [11:0] rom_2_data;
  wire [19:0] register_3_q, rom_1_data;

  Clock clock_1 (.out(clock_1_out));
  Register register_1 (.Q(register_1_q), .clk(clock_1_out));  // open: D, en, clr
  ROM #(.dataWidth(20)) rom_1 (.addr(register_1_q), .data(rom_1_data));  // open: sel
  Register register_2 (.clk(clock_1_out));  // open: D, en, Q, clr
  Register #(.width(20)) register_3 (.D(rom_1_data), .Q(register_3_q), .clk(clock_1_out));  // open: en, clr
  ROM #(.addrWidth(4), .dataWidth(12)) rom_2 (.addr(register_3_q[19:16]), .data(rom_2_data));  // open: sel
  Register_File register_file_1 (
    .Write_Data(register_13_q), .Read_Reg1(register_3_q[15:12]), .Read_Reg2(register_3_q[11:8]),
    .Write_Reg(register_14_q), .Reg_clock(clock_1_out), .RegWrite(rom_2_data[8]),
    .Read_Data_1(register_file_1_read_data_1), .Read_Data_2(register_file_1_read_data_2));  // open: Error_Write_to_0
  Register #(.width(3)) register_4 (.D(rom_2_data[2:0]), .Q(register_4_q), .clk(clock_1_out));  // open: en, clr
  Register #(.width(2)) register_5 (.D(rom_2_data[7:6]), .Q(register_5_q), .clk(clock_1_out));  // open: en, clr
  Register register_6 (.D(register_file_1_read_data_1), .Q(register_6_q), .clk(clock_1_out));  // open: en, clr
  Register register_7 (.D(register_file_1_read_data_2), .Q(register_7_q), .clk(clock_1_out));  // open: en, clr
  Register #(.width(4)) register_8 (.D(register_3_q[7:4]), .Q(register_8_q), .clk(clock_1_out));  // open: en, clr
  ALU alu_1 (.A(register_6_q), .B(register_7_q), .ALUop(register_4_q), .F(alu_1_f));  // open: overflow, negative, ZF
  Register #(.width(2)) register_9 (.D(register_5_q), .Q(register_9_q), .clk(clock_1_out));  // open: en, clr
  Register register_10 (.D(alu_1_f), .Q(register_10_q), .clk(clock_1_out));  // open: en, clr
  Register register_11 (.D(register_7_q), .Q(register_11_q), .clk(clock_1_out));  // open: en, clr
  Register #(.width(4)) register_12 (.D(register_8_q), .Q(register_12_q), .clk(clock_1_out));  // open: en, clr
  RAM #(.bus("separate")) ram_1 (
    .addr(register_10_q), .din(register_11_q), .str(register_9_q[0]), .clk(clock_1_out), .ld(register_9_q[1]));  // open: data, sel, clr
  Register register_13 (.D(register_10_q), .Q(register_13_q), .clk(clock_1_out));  // open: en, clr
  Register #(.width(4)) register_14 (.D(register_12_q), .Q(register_14_q), .clk(clock_1_out));  // open: en, clr

  // Notes on the sheet:
  //   contents of rom_1 (hex, n*v repeats v):
  //   43420 d3510 62150 f3420 54420 32a e0542 832fc 732f6 b32f6 332f6 932fc a530a 96200 86601 a6300 76601
  //   23200 114f3 c0000 c0700 c1300
  //   contents of rom_2 (hex, n*v repeats v):
  //   f05 31 21 302 500 504 503 300 301 240 380 303 f 501 f06 502
  //   RegWrite
  //   ALUOp
  //   MemWrite
  //   MemRead
endmodule
